# Fritzing sketch fritzing final sketch (saved by Fritzing 0.9.3b)
breadboards: 1

parts:
  Part1 = Arduino Uno (Rev3)
  TFT1 = Color 320x240 TFT Display, ILI9341 Controller Chip  # not connected
  ZS-042_RTC1 = ZS-042 RTC Module
  S1 = Pushbutton [package="[THT]"]
  VCC1 = 4 x AAA Battery Mount
  WeMos_D1_Mini_Relay_Shield1 = WeMos D1 Mini Relay Shield
  LED1 = smd LED [color="Red (633nm)" package="0603 [SMD]"]
  R1 = Resistor [tolerance=±5% resistance=220 package=THT]

nets:
  N1: Part1.A4/SDA, ZS-042_RTC1.SDA
  N2: Part1.A5/SCL, ZS-042_RTC1.SCL
  N3: Part1.D2, R1.Pin_0
  N4: Part1.D4, ZS-042_RTC1.VCC
  N5: Part1.D7, WeMos_D1_Mini_Relay_Shield1.RX
  5V: Part1.5V, VCC1.+, WeMos_D1_Mini_Relay_Shield1.5V
  GND: Part1.GND, ZS-042_RTC1.GND, S1.Pin_1, S1.Pin_2, WeMos_D1_Mini_Relay_Shield1.COM, WeMos_D1_Mini_Relay_Shield1.D3, LED1.cathode
  N6: S1.Pin_3, S1.Pin_4, VCC1.-, WeMos_D1_Mini_Relay_Shield1.NO

notes:
  LED
  SCK
  SDA
  A0
  RESET
  CS
  GND
  VCC
  128x60 spi ST7735

custom parts:
  Color 320x240 TFT Display, ILI9341 Controller Chip: 2.2" TFT Display with ILI9341 Controller
